// Logisim project PCOAssignment.circ as structural Verilog: 10 circuits, main circuit 19071110main
module _19071110main (
);

  _19071110ALU u_19071110alu_1 ();  // open: A, B, sel, out, out_5
endmodule

// ALU
module _19071110ALU (
  input  [31:0] A,
  input  [31:0] B,
  input  [1:0] sel,
  output [31:0] out,
  output out_5
);

  wire [31:0] and_1_out, n19071110adder_1_sum, n19071110subtractor_1_difference, or_1_out;

  _19071110Adder u_19071110adder_1 (.B(A), .A(B), .Cin(1'b0), .sum(n19071110adder_1_sum));  // open: Cout
  _19071110Subtractor u_19071110subtractor_1 (
    .X(A), .Y(B), .Bin(1'b0), .difference(n19071110subtractor_1_difference));  // open: Bout
  assign and_1_out = A & B;  // AND_Gate and_1, 32 bits wide
  assign or_1_out = A | B;  // OR_Gate or_1, 32 bits wide
  Multiplexer #(.select(2), .width(32), .disabled("Z"), .enable("false")) multiplexer_1 (
    .in0(n19071110adder_1_sum), .in1(n19071110subtractor_1_difference), .in2(and_1_out), .in3(or_1_out),
    .out(out), .sel(sel));
  _19071110IsZero u_19071110iszero_1 (.x(out), .zero(out_5));
endmodule

// IsZero
module _19071110IsZero (
  input  [31:0] x,
  output zero
);

  wire [1:0] or_4_out;
  wire [3:0] or_2_out;
  wire [7:0] or_3_out;
  wire [15:0] or_1_out;

  assign or_1_out = x[15:0] | x[31:16];  // OR_Gate or_1, 16 bits wide
  assign or_2_out = or_3_out[3:0] | or_3_out[7:4];  // OR_Gate or_2, 4 bits wide
  assign or_3_out = or_1_out[7:0] | or_1_out[15:8];  // OR_Gate or_3, 8 bits wide
  assign or_4_out = or_2_out[1:0] | or_2_out[3:2];  // OR_Gate or_4, 2 bits wide
  nor nor_1 (zero, or_4_out[0], or_4_out[1]);
endmodule

// Sub
module _19071110Subtractor (
  input  [31:0] X,
  input  [31:0] Y,
  input  Bin,
  output [31:0] difference,
  output Bout
);

  wire n19071110adder_1_cout, not_2_out;
  wire [31:0] not_1_out;

  assign not_1_out = ~Y;  // NOT_Gate not_1, 32 bits wide
  _19071110Adder u_19071110adder_1 (
    .B(X), .A(not_1_out), .Cin(not_2_out), .sum(difference), .Cout(n19071110adder_1_cout));
  not not_2 (not_2_out, Bin);
  not not_3 (Bout, n19071110adder_1_cout);
endmodule

// Adder
module _19071110Adder (
  input  [31:0] B,
  input  [31:0] A,
  input  Cin,
  output [31:0] sum,
  output Cout
);

  wire [5:0] bit_extender_1_out, bit_extender_2_out, n19071110abtog_p_6_g_star, n19071110abtog_p_6_p_star,
       n19071110adder6_1_sum, n19071110carrygenerator_1_carry;

  assign bit_extender_1_out = {{4{A[31]}}, A[31:30]};  // Bit_Extender bit_extender_1
  assign bit_extender_2_out = {{4{B[31]}}, B[31:30]};  // Bit_Extender bit_extender_2
  _19071110ABToG_P u_19071110abtog_p_1 (
    .A(bit_extender_1_out), .B(bit_extender_2_out), .P_star(n19071110abtog_p_6_p_star[5]),
    .G_star(n19071110abtog_p_6_g_star[5]));
  _19071110ABToG_P u_19071110abtog_p_2 (
    .A(A[29:24]), .B(B[29:24]), .P_star(n19071110abtog_p_6_p_star[4]), .G_star(n19071110abtog_p_6_g_star[4]));
  _19071110ABToG_P u_19071110abtog_p_3 (
    .A(A[23:18]), .B(B[23:18]), .P_star(n19071110abtog_p_6_p_star[3]), .G_star(n19071110abtog_p_6_g_star[3]));
  _19071110ABToG_P u_19071110abtog_p_4 (
    .A(A[17:12]), .B(B[17:12]), .P_star(n19071110abtog_p_6_p_star[2]), .G_star(n19071110abtog_p_6_g_star[2]));
  _19071110ABToG_P u_19071110abtog_p_5 (
    .A(A[11:6]), .B(B[11:6]), .P_star(n19071110abtog_p_6_p_star[1]), .G_star(n19071110abtog_p_6_g_star[1]));
  _19071110ABToG_P u_19071110abtog_p_6 (
    .A(A[5:0]), .B(B[5:0]), .P_star(n19071110abtog_p_6_p_star[0]), .G_star(n19071110abtog_p_6_g_star[0]));
  Bit_Extender #(.in_width(6), .out_width(2), .\type ("sign")) bit_extender_3 (
    .in(n19071110adder6_1_sum), .out(sum[31:30]));
  _19071110Adder6 u_19071110adder6_1 (
    .Cin(n19071110carrygenerator_1_carry[5]), .A(bit_extender_1_out), .B(bit_extender_2_out),
    .sum(n19071110adder6_1_sum));  // open: Cout
  _19071110Adder6 u_19071110adder6_2 (
    .Cin(n19071110carrygenerator_1_carry[4]), .A(A[29:24]), .B(B[29:24]), .sum(sum[29:24]));  // open: Cout
  _19071110Adder6 u_19071110adder6_3 (
    .Cin(n19071110carrygenerator_1_carry[3]), .A(A[23:18]), .B(B[23:18]), .sum(sum[23:18]));  // open: Cout
  _19071110Adder6 u_19071110adder6_4 (
    .Cin(n19071110carrygenerator_1_carry[2]), .A(A[17:12]), .B(B[17:12]), .sum(sum[17:12]));  // open: Cout
  _19071110Adder6 u_19071110adder6_5 (
    .Cin(n19071110carrygenerator_1_carry[1]), .A(A[11:6]), .B(B[11:6]), .sum(sum[11:6]));  // open: Cout
  _19071110Adder6 u_19071110adder6_6 (
    .Cin(n19071110carrygenerator_1_carry[0]), .A(A[5:0]), .B(B[5:0]), .sum(sum[5:0]));  // open: Cout
  _19071110CarryGenerator u_19071110carrygenerator_1 (
    .G(n19071110abtog_p_6_g_star), .P(n19071110abtog_p_6_p_star), .Cin(Cin),
    .carry(n19071110carrygenerator_1_carry), .Cout(Cout));
endmodule

// Adder6
module _19071110Adder6 (
  input  [5:0] A,
  input  [5:0] B,
  input  Cin,
  output [5:0] sum,
  output Cout
);

  wire [5:0] n19071110abtogp_6_g, n19071110abtogp_6_p, n19071110carrygenerator_1_carry;

  _19071110ABToGP u_19071110abtogp_1 (.A(A[5]), .B(B[5]), .G(n19071110abtogp_6_g[5]), .P(n19071110abtogp_6_p[5]));
  _19071110ABToGP u_19071110abtogp_2 (.A(A[4]), .B(B[4]), .G(n19071110abtogp_6_g[4]), .P(n19071110abtogp_6_p[4]));
  _19071110ABToGP u_19071110abtogp_3 (.A(A[3]), .B(B[3]), .G(n19071110abtogp_6_g[3]), .P(n19071110abtogp_6_p[3]));
  _19071110ABToGP u_19071110abtogp_4 (.A(A[2]), .B(B[2]), .G(n19071110abtogp_6_g[2]), .P(n19071110abtogp_6_p[2]));
  _19071110ABToGP u_19071110abtogp_5 (.A(A[1]), .B(B[1]), .G(n19071110abtogp_6_g[1]), .P(n19071110abtogp_6_p[1]));
  _19071110ABToGP u_19071110abtogp_6 (.A(A[0]), .B(B[0]), .G(n19071110abtogp_6_g[0]), .P(n19071110abtogp_6_p[0]));
  _19071110Adder1 u_19071110adder1_1 (
    .A(A[5]), .B(B[5]), .Cin(n19071110carrygenerator_1_carry[5]), .S(sum[5]));  // open: Cout
  _19071110Adder1 u_19071110adder1_2 (
    .A(A[4]), .B(B[4]), .Cin(n19071110carrygenerator_1_carry[4]), .S(sum[4]));  // open: Cout
  _19071110Adder1 u_19071110adder1_3 (
    .A(A[3]), .B(B[3]), .Cin(n19071110carrygenerator_1_carry[3]), .S(sum[3]));  // open: Cout
  _19071110Adder1 u_19071110adder1_4 (
    .A(A[2]), .B(B[2]), .Cin(n19071110carrygenerator_1_carry[2]), .S(sum[2]));  // open: Cout
  _19071110Adder1 u_19071110adder1_5 (
    .A(A[1]), .B(B[1]), .Cin(n19071110carrygenerator_1_carry[1]), .S(sum[1]));  // open: Cout
  _19071110Adder1 u_19071110adder1_6 (
    .A(A[0]), .B(B[0]), .Cin(n19071110carrygenerator_1_carry[0]), .S(sum[0]));  // open: Cout
  _19071110CarryGenerator u_19071110carrygenerator_1 (
    .G(n19071110abtogp_6_g), .P(n19071110abtogp_6_p), .Cin(Cin), .carry(n19071110carrygenerator_1_carry),
    .Cout(Cout));
endmodule

// Adder1
module _19071110Adder1 (
  input  A,
  input  B,
  input  Cin,
  output S,
  output Cout
);

  wire and_1_out, and_2_out, xor_1_out;

  xor xor_1 (xor_1_out, A, B);
  and and_1 (and_1_out, A, B);
  xor xor_2 (S, xor_1_out, Cin);
  and and_2 (and_2_out, xor_1_out, Cin);
  or or_1 (Cout, and_2_out, and_1_out);
endmodule

// CarryGen
module _19071110CarryGenerator (
  input  [5:0] G,
  input  [5:0] P,
  input  Cin,
  output [5:0] carry,
  output Cout
);

  wire and_1_out, and_2_out, and_3_out, and_4_out, and_5_out, and_6_out, and_7_out, and_8_out, and_9_out,
       and_10_out, and_11_out, and_12_out, and_13_out, and_14_out, and_15_out, and_16_out, and_17_out,
       and_18_out, and_19_out, and_20_out, and_21_out;

  and and_1 (and_1_out, P[5], and_4_out);
  and and_2 (and_2_out, P[5], and_3_out);
  and and_3 (and_3_out, P[4], and_5_out);
  and and_4 (and_4_out, P[4], and_6_out);
  and and_5 (and_5_out, P[3], and_8_out);
  and and_6 (and_6_out, P[3], and_7_out);
  and and_7 (and_7_out, P[2], and_10_out);
  and and_8 (and_8_out, P[2], and_9_out);
  and and_9 (and_9_out, P[1], G[0]);
  and and_10 (and_10_out, P[1], and_11_out);
  and and_11 (and_11_out, Cin, P[0]);
  and and_12 (and_12_out, P[5], and_13_out);
  and and_13 (and_13_out, P[4], and_14_out);
  and and_14 (and_14_out, P[3], and_15_out);
  and and_15 (and_15_out, P[2], G[1]);
  and and_16 (and_16_out, P[5], and_18_out);
  and and_17 (and_17_out, P[5], and_19_out);
  and and_18 (and_18_out, P[4], and_20_out);
  and and_19 (and_19_out, P[4], G[3]);
  and and_20 (and_20_out, P[3], G[2]);
  and and_21 (and_21_out, P[5], G[4]);
  or or_1 (Cout, G[5], and_21_out, and_17_out, and_16_out, and_12_out, and_2_out, and_1_out);
  or or_2 (carry[5], G[4], and_19_out, and_18_out, and_13_out, and_3_out, and_4_out);
  or or_3 (carry[4], G[3], and_20_out, and_14_out, and_5_out, and_6_out);
  or or_4 (carry[3], G[2], and_15_out, and_8_out, and_7_out);
  or or_5 (carry[2], G[1], and_9_out, and_10_out);
  or or_6 (carry[1], G[0], and_11_out);

  assign carry[0] = Cin;
endmodule

// ABG*P*
module _19071110ABToG_P (
  input  [5:0] A,
  input  [5:0] B,
  output P_star,
  output G_star
);

  wire and_1_out, and_2_out, and_3_out, and_4_out, and_5_out, and_6_out, and_7_out, and_8_out, and_9_out,
       n19071110abtogp_1_g, n19071110abtogp_1_p, n19071110abtogp_2_g, n19071110abtogp_2_p,
       n19071110abtogp_3_g, n19071110abtogp_3_p, n19071110abtogp_4_g, n19071110abtogp_4_p,
       n19071110abtogp_5_g, n19071110abtogp_5_p, n19071110abtogp_6_g, n19071110abtogp_6_p;

  _19071110ABToGP u_19071110abtogp_1 (.A(A[5]), .B(B[5]), .G(n19071110abtogp_1_g), .P(n19071110abtogp_1_p));
  _19071110ABToGP u_19071110abtogp_2 (.A(A[4]), .B(B[4]), .G(n19071110abtogp_2_g), .P(n19071110abtogp_2_p));
  _19071110ABToGP u_19071110abtogp_3 (.A(A[3]), .B(B[3]), .G(n19071110abtogp_3_g), .P(n19071110abtogp_3_p));
  _19071110ABToGP u_19071110abtogp_4 (.A(A[2]), .B(B[2]), .G(n19071110abtogp_4_g), .P(n19071110abtogp_4_p));
  _19071110ABToGP u_19071110abtogp_5 (.A(A[1]), .B(B[1]), .G(n19071110abtogp_5_g), .P(n19071110abtogp_5_p));
  _19071110ABToGP u_19071110abtogp_6 (.A(A[0]), .B(B[0]), .G(n19071110abtogp_6_g), .P(n19071110abtogp_6_p));
  and and_1 (and_1_out, n19071110abtogp_5_p, and_4_out);
  and and_2 (and_2_out, and_1_out, n19071110abtogp_6_g);
  and and_3 (and_3_out, n19071110abtogp_3_p, and_7_out);
  and and_4 (and_4_out, n19071110abtogp_4_p, and_3_out);
  and and_5 (and_5_out, and_4_out, n19071110abtogp_5_g);
  and and_6 (and_6_out, and_3_out, n19071110abtogp_4_g);
  and and_7 (and_7_out, n19071110abtogp_2_p, n19071110abtogp_1_p);
  and and_8 (and_8_out, n19071110abtogp_1_p, n19071110abtogp_2_g);
  and and_9 (and_9_out, and_7_out, n19071110abtogp_3_g);
  and and_10 (P_star, n19071110abtogp_6_p, n19071110abtogp_5_p, n19071110abtogp_4_p, n19071110abtogp_3_p, n19071110abtogp_2_p, n19071110abtogp_1_p);
  or or_1 (G_star, n19071110abtogp_1_g, and_8_out, and_9_out, and_6_out, and_5_out, and_2_out);
endmodule

// ABGP
module _19071110ABToGP (
  input  A,
  input  B,
  output G,
  output P
);

  and and_1 (G, A, B);
  xor xor_1 (P, B, A);
endmodule
